// Logisim project ex4.circ as structural Verilog: 1 circuit, main circuit SplitThing
module SplitThing (
  input  [7:0] INPUT0,
  output OUTPUT0,
  output [7:0] OUTPUT1
);

  not not_1 (OUTPUT1[7], INPUT0[7]);
  and and_1 (OUTPUT0, INPUT0[0], INPUT0[7]);

  assign OUTPUT1[6:0] = INPUT0[6:0];
endmodule
