// Logisim project ex5.circ as structural Verilog: 5 circuits, main circuit RotRight
module RotRight (
  input  [15:0] INPUT0,
  input  [3:0] AMOUNT,
  output [15:0] OUTPUT0
);

  wire [15:0] rot2input, rot4input, rot8input;

  Multiplexer #(.enable("false"), .width(16)) multiplexer_1 (
    .in0(rot2input), .in1({rot2input[1:0], rot2input[15:2]}), .out(rot4input), .sel(AMOUNT[1]));
  Multiplexer #(.enable("false"), .width(16)) multiplexer_2 (
    .in0(INPUT0), .in1({INPUT0[0], INPUT0[15:1]}), .out(rot2input), .sel(AMOUNT[0]));
  Multiplexer #(.enable("false"), .width(16)) multiplexer_3 (
    .in0(rot4input), .in1({rot4input[3:0], rot4input[15:4]}), .out(rot8input), .sel(AMOUNT[2]));
  Multiplexer #(.enable("false"), .width(16)) multiplexer_4 (
    .in0(rot8input), .in1({rot8input[7:0], rot8input[15:8]}), .out(OUTPUT0), .sel(AMOUNT[3]));

  // Other names for the same wires on the sheet: rot1input[15:0] = INPUT0;
  //   rot1output[15:0] = {INPUT0[0], INPUT0[15:1]}; rot2output[15:0] = {rot2input[1:0], rot2input[15:2]};
  //   rot4output[15:0] = {rot4input[3:0], rot4input[15:4]}; rot8output[15:0] = {rot8input[7:0], rot8input[15:8]}
endmodule

module rot1 (
  input  [15:0] in_1,
  output [15:0] out_2
);


  assign out_2 = {in_1[0], in_1[15:1]};

  // Other names for the same wires on the sheet: rot1input[15:0] = in_1; rot1output[15:0] = {in_1[0], in_1[15:1]}
endmodule

module rot2 (
  input  [15:0] in_1,
  output [15:0] out_2
);


  assign out_2 = {in_1[1:0], in_1[15:2]};

  // Other names for the same wires on the sheet: rot2input[15:0] = in_1; rot2output[15:0] = {in_1[1:0], in_1[15:2]}
endmodule

module rot4 (
  input  [15:0] in_1,
  output [15:0] out_2
);


  assign out_2 = {in_1[3:0], in_1[15:4]};

  // Other names for the same wires on the sheet: rot4input[15:0] = in_1; rot4output[15:0] = {in_1[3:0], in_1[15:4]}
endmodule

module rot8 (
  input  [15:0] in_1,
  output [15:0] out_2
);


  assign out_2 = {in_1[7:0], in_1[15:8]};

  // Other names for the same wires on the sheet: rot8input[15:0] = in_1; rot8output[15:0] = {in_1[7:0], in_1[15:8]}
endmodule
