// Logisim project ex2.circ as structural Verilog: 1 circuit, main circuit pipelined
module pipelined (
  input  [7:0] in1,
  input  [7:0] in2,
  input  CLK,
  output [7:0] out1
);

  wire [7:0] adder_1_out, multiplier_1_out, register_1_q;

  Multiplier multiplier_1 (.a(in1), .b(in2), .out(multiplier_1_out));  // open: cin, cout
  // Probe on multiplier_1_out
  Register register_1 (.D(multiplier_1_out), .clk(CLK), .Q(register_1_q));  // open: en, clr
  // Probe on register_1_q
  // Probe on adder_1_out
  Adder adder_1 (.a(register_1_q), .b(out1), .out(adder_1_out));  // open: cin, cout
  Register register_2 (.D(adder_1_out), .clk(CLK), .Q(out1));  // open: en, clr
  // Probe on out1
endmodule
