// Logisim project alu.circ as structural Verilog: 1 circuit, main circuit alu
module alu (
  input  [31:0] A,
  input  [31:0] B,
  input  [3:0] ALUSel,
  output [31:0] Result,
  output [31:0] out_5,
  output [31:0] out_6
);

  wire slt2;
  wire [31:0] add0, and7, and_1_out, and_2_out, and_3_out, mul8, mulh9, mulhu11, or6, sra13, sub12, xor4;

  assign and_1_out = B & 32'h1f;  // AND_Gate and_1, 32 bits wide
  assign and_2_out = B & 32'h1f;  // AND_Gate and_2, 32 bits wide
  assign and_3_out = B & 32'h1f;  // AND_Gate and_3, 32 bits wide
  Adder #(.width(32)) adder_1 (.a(A), .b(B), .out(add0));  // open: cin, cout
  Comparator #(.width(32)) comparator_1 (.a(A), .b(B), .lt(slt2));  // open: gt, eq
  assign xor4 = A ^ B;  // XOR_Gate xor_1, 32 bits wide
  Shifter #(.width(32)) shifter_1 (.in(A), .\dist (and_1_out[4:0]), .out(out_5));
  Shifter #(.shift("lr"), .width(32)) shifter_2 (.in(A), .\dist (and_2_out[4:0]), .out(out_6));
  assign or6 = A | B;  // OR_Gate or_1, 32 bits wide
  assign and7 = A & B;  // AND_Gate and_4, 32 bits wide
  Multiplier #(.mode("twosComplement"), .width(32)) multiplier_1 (.a(A), .b(B), .out(mul8));  // open: cin, cout
  Multiplier #(.mode("twosComplement"), .width(32)) multiplier_2 (.a(A), .b(B), .cout(mulh9));  // open: out, cin
  Multiplier #(.width(32)) multiplier_3 (.a(A), .b(B), .cout(mulhu11));  // open: out, cin
  Subtractor #(.width(32)) subtractor_1 (.a(A), .b(B), .out(sub12));  // open: bin, bout
  Shifter #(.shift("ar"), .width(32)) shifter_3 (.in(A), .\dist (and_3_out[4:0]), .out(sra13));
  Multiplexer #(.enable("false"), .select(4), .width(32)) multiplexer_1 (
    .in0(add0), .in1(out_5), .in2({{31{1'b0}}, slt2}), .in4(xor4), .in5(out_6), .in6(or6), .in7(and7),
    .in8(mul8), .in9(mulh9), .in11(mulhu11), .in12(sub12), .in13(sra13), .in15(B), .out(Result), .sel(ALUSel));  // open: in3, in10, in14

  // Other names for the same wires on the sheet: bsel[31:0] = B; sll1[31:0] = out_5; srl5[31:0] = out_6

  // Notes on the sheet:
  //   INPUTS to your circuit
  //   ADD
  //   shift left
  //   set less than
  //   DON'T CHANGE THE LOCATIONS OF THE INPUTS AND OUTPUTS!
  //   OUTPUT from your circuit
endmodule
