// Logisim project control-logic.circ as structural Verilog: 1 circuit, main circuit control_logic
module control_logic (
  input  [31:0] inst,
  input  BrEq,
  input  BrLt,
  output PCSel,
  output RegWEn,
  output [2:0] ImmSel,
  output BrUn,
  output ASel,
  output BSel,
  output [3:0] ALUSel,
  output MemRW,
  output [1:0] WBSel,
  output CSRSel,
  output CSRWen
);

  wire and_1_out, and_2_out, and_3_out, and_4_out, and_5_out, and_6_out, and_38_out, and_39_out, and_40_out,
       and_41_out, and_42_out, and_43_out, if_do_condition_jump, is_addi, is_and, is_andi, is_auipc, is_beq,
       is_bge, is_bgeu, is_blt, is_bltu, is_bne, is_CSRRWI, is_I_type, is_I_type_0x03, is_I_type_0x67,
       is_I_type_0x73, is_jal, is_lui, is_mul, is_mulh, is_mulhu, is_or, is_ori, is_SB_type, is_sll, is_slli,
       is_slt, is_slti, is_sra, is_srai, is_srl, is_srli, is_sub, is_U_type, is_xor, is_xori, or_7_out,
       or_13_out;

  and and_1 (and_1_out, ~inst[12], ~inst[13], ~inst[14]);  // AND_Gate
  and and_2 (and_2_out, inst[12], ~inst[13], ~inst[14]);  // AND_Gate
  and and_3 (and_3_out, ~inst[12], ~inst[13], inst[14]);  // AND_Gate
  and and_4 (and_4_out, inst[12], ~inst[13], inst[14]);  // AND_Gate
  and and_5 (and_5_out, ~inst[12], inst[13], inst[14]);  // AND_Gate
  and and_6 (and_6_out, inst[12], inst[13], inst[14]);
  and and_7 (is_beq, is_SB_type, and_1_out);
  and and_8 (is_bne, is_SB_type, and_2_out);
  and and_9 (is_blt, is_SB_type, and_3_out);
  and and_10 (is_bge, is_SB_type, and_4_out);
  and and_11 (is_bltu, is_SB_type, and_5_out);
  and and_12 (is_bgeu, and_6_out, is_SB_type);
  and and_13 (is_sll, inst[12], BSel);
  and and_14 (is_mulh, inst[12], inst[25], BSel);
  and and_15 (is_srl, inst[14], inst[12], BSel);
  and and_16 (is_slli, inst[12], is_addi);
  Priority_Encoder priority_encoder_1 (
    .in0(is_I_type), .in1(is_U_type), .in2(MemRW), .in3(is_SB_type), .in4(is_jal), .in5(BSel), .out(ImmSel));  // open: in6, in7, en_in, gs, en_out
  and and_17 (is_mulhu, inst[13], inst[14], inst[25], BSel);
  and and_18 (is_sra, inst[14], inst[12], inst[30], BSel);
  and and_19 (is_and, inst[12], inst[13], inst[14], BSel);
  and and_20 (is_srli, inst[14], inst[12], is_addi);
  and and_21 (is_srai, inst[14], inst[12], is_addi, inst[30]);
  and and_22 (is_andi, inst[12], inst[13], inst[14], is_addi);
  and and_23 (CSRSel, is_I_type_0x73, inst[12], ~inst[13], ~inst[14]);  // AND_Gate
  and and_24 (is_I_type_0x03, inst[0], inst[1], ~inst[2], ~inst[3], ~inst[4], ~inst[5], ~inst[6]);  // AND_Gate
  and and_25 (is_addi, inst[0], inst[1], ~inst[2], ~inst[3], inst[4], ~inst[5], ~inst[6]);  // AND_Gate
  and and_26 (is_I_type_0x67, inst[0], inst[1], inst[2], ~inst[3], ~inst[4], inst[5], inst[6]);  // AND_Gate
  and and_27 (is_I_type_0x73, inst[0], inst[1], ~inst[2], ~inst[3], inst[4], inst[5], inst[6]);  // AND_Gate
  and and_28 (is_auipc, inst[0], inst[1], inst[2], ~inst[3], inst[4], ~inst[5], ~inst[6]);  // AND_Gate
  and and_29 (is_sub, inst[30], BSel);
  and and_30 (is_xor, inst[14], BSel);
  and and_31 (is_slt, inst[13], BSel);
  and and_32 (is_or, inst[13], inst[14], BSel);
  and and_33 (is_slti, inst[13], is_addi);
  and and_34 (is_ori, inst[13], inst[14], is_addi);
  and and_35 (is_xori, inst[14], is_addi);
  and and_36 (is_mul, inst[25], BSel);
  or or_1 (WBSel[1], is_jal, is_I_type_0x67);
  or or_2 (WBSel[0], is_slt, is_sub, BSel, is_mul, is_sll, is_mulh, is_mulhu, is_xor, is_srl, is_sra, is_or, is_and, is_addi, is_slli, is_slti, is_xori, is_srli, is_srai, is_ori, is_andi, is_auipc, is_lui);
  and and_37 (is_CSRRWI, is_I_type_0x73, inst[12], ~inst[13], inst[14]);  // AND_Gate
  and and_38 (and_38_out, is_beq, BrEq);
  and and_39 (and_39_out, is_bne, ~BrEq);  // AND_Gate
  and and_40 (and_40_out, is_blt, BrLt);
  and and_41 (and_41_out, is_bge, ~BrLt);  // AND_Gate
  and and_42 (and_42_out, is_bltu, BrUn, BrLt);
  and and_43 (and_43_out, is_bgeu, BrUn, BrLt);
  and and_44 (is_SB_type, inst[0], inst[1], ~inst[2], ~inst[3], ~inst[4], inst[5], inst[6]);  // AND_Gate
  and and_45 (is_jal, inst[0], inst[1], inst[2], inst[3], ~inst[4], inst[5], inst[6]);  // AND_Gate
  or or_3 (ALUSel[1], is_mulhu, is_slt, is_or, is_and, is_slti, is_ori, is_andi, is_lui);
  or or_4 (ALUSel[2], is_sub, is_xor, is_srl, is_sra, is_or, is_and, is_xori, is_srli, is_srai, is_ori, is_andi, is_lui);
  or or_5 (ALUSel[3], is_mul, is_sub, is_mulh, is_mulhu, is_sra, is_srai, is_lui);
  or or_6 (if_do_condition_jump, and_38_out, and_39_out, and_40_out, and_41_out, and_42_out, and_43_out);
  or or_7 (or_7_out, is_SB_type, MemRW);
  not not_1 (RegWEn, or_7_out);
  or or_8 (ALUSel[0], is_sll, is_mulh, is_mulhu, is_srl, is_sra, is_and, is_slli, is_srli, is_srai, is_andi, is_lui);
  or or_9 (PCSel, if_do_condition_jump, is_I_type_0x67, is_jal);
  or or_10 (is_I_type, is_I_type_0x03, is_addi, is_I_type_0x67, is_I_type_0x73);
  or or_11 (is_U_type, is_lui, is_auipc);
  // Probe on ALUSel
  and and_46 (is_lui, inst[0], inst[1], inst[2], ~inst[3], inst[4], inst[5], ~inst[6]);  // AND_Gate
  and and_47 (is_auipc, inst[0], inst[1], inst[2], ~inst[3], inst[4], ~inst[5], ~inst[6]);  // AND_Gate
  and and_48 (BSel, inst[0], inst[1], ~inst[2], ~inst[3], inst[4], inst[5], ~inst[6]);  // AND_Gate
  and and_49 (MemRW, inst[0], inst[1], ~inst[2], ~inst[3], ~inst[4], inst[5], ~inst[6]);  // AND_Gate
  or or_12 (BrUn, is_bltu, is_bgeu);
  or or_13 (or_13_out, is_SB_type, is_jal, is_auipc);
  not not_2 (ASel, or_13_out);

  assign CSRWen = 1'b1;

  // Other names for the same wires on the sheet: alu_xxx1 = ALUSel[0]; alu_xx1x = ALUSel[1]; alu_x1xx = ALUSel[2];
  //   alu_1xxx = ALUSel[3]; opcode[6:0] = inst[6:0]; opcode_0 = inst[0]; opcode_1 = inst[1]; opcode_2 = inst[2];
  //   opcode_3 = inst[3]; opcode_4 = inst[4]; opcode_5 = inst[5]; opcode_6 = inst[6]; rd[4:0] = inst[11:7];
  //   funct3[2:0] = inst[14:12]; funct3_0 = inst[12]; funct3_1 = inst[13]; funct3_2 = inst[14];
  //   rs1[4:0] = inst[19:15]; imm[11:0] = inst[31:20]; rs2[4:0] = inst[24:20]; funct7[6:0] = inst[31:25];
  //   funct7_0 = inst[25]; immed[6:0] = inst[31:25]; funct7_1 = inst[26]; funct7_2 = inst[27]; funct7_3 = inst[28];
  //   funct7_4 = inst[29]; funct7_5 = inst[30]; funct7_6 = inst[31]; is_add = BSel; is_R_type = BSel;
  //   is_I_type_0x13 = is_addi; is_U_type_0x17 = is_auipc; is_CSRRW = CSRSel; is_UJ_type = is_jal;
  //   is_jalr = is_I_type_0x67; is_U_type_0x37 = is_lui; is_S_type = MemRW; WBSel_x1 = WBSel[0]; WBSel_1x = WBSel[1]

  // Notes on the sheet:
  //   INPUTS to your circuit
  //   DON'T CHANGE THE LOCATIONS OF THE INPUTS AND OUTPUTS!
  //   OUTPUT from your circuit
  //   PCSel
  //   BrUn
endmodule
