// Logisim project cpu.circ as structural Verilog: 1 circuit, main circuit cpu
module cpu (
  input  clk,
  input  [31:0] INSTRUCTION,
  input  [31:0] READ_DATA,
  output [31:0] WRITE_ADDRESS,
  output [31:0] PROGRAM_COUNTER,
  output [31:0] ra,
  output [31:0] sp,
  output [31:0] t0,
  output [31:0] t1,
  output [31:0] t2,
  output [31:0] s0,
  output [31:0] s1,
  output [31:0] a0,
  output [31:0] tohost,
  output [3:0] WRITE_ENABLE,
  output [31:0] WRITE_DATA
);

  wire ASel, breq, brlt, brun, BSel, CSRSel, CSRWen, jal, jalr, MemRW, PCSel, RegWEn;
  wire [1:0] WBSel;
  wire [2:0] control_logic_1_immsel;
  wire [3:0] ALUSel;
  wire [4:0] imm_20_31;
  wire [6:0] funct7;
  wire [19:0] INSTRUCTION_AFTER;
  wire [31:0] bit_extender_2_out, CSR_din, imm, multiplexer_1_out, multiplexer_3_out, multiplexer_4_out,
       multiplexer_5_out, PC_AFTER, pcplus4, rs1_data, WB;

  // Probe on pcplus4
  Adder #(.width(32)) adder_1 (.a(PROGRAM_COUNTER), .b(32'h4), .out(pcplus4));  // open: cin, cout
  Multiplexer #(.width(32)) multiplexer_1 (.in0(pcplus4), .in1(WRITE_ADDRESS), .out(multiplexer_1_out), .sel(PCSel));
  // Probe on WB
  Register #(.width(32)) PC (.D(multiplexer_1_out), .en(1'b1), .clk(clk), .Q(PROGRAM_COUNTER));  // open: clr
  Multiplexer #(.select(2), .width(32)) multiplexer_2 (
    .in0(READ_DATA), .in1(WRITE_ADDRESS), .in2(PROGRAM_COUNTER), .out(WB), .sel(WBSel));  // open: in3
  regfile regfile_1 (
    .rs1(INSTRUCTION_AFTER[19:15]), .rs2(imm_20_31), .rd(INSTRUCTION_AFTER[11:7]), .Write_Data(WB),
    .RegWEn(RegWEn), .clk(clk), .ra(ra), .sp(sp), .t0(t0), .t1(t1), .t2(t2), .s0(s0), .s1(s1), .a0(a0),
    .Read_Data_1(rs1_data), .Read_Data_2(WRITE_DATA));
  branch_comp branch_comp_1 (.rs1(rs1_data), .rs2(WRITE_DATA), .BrUn(brun), .BrEq(breq), .BrLt(brlt));
  // Probe on imm
  imm_gen imm_gen_1 (.inst({funct7, imm_20_31, INSTRUCTION_AFTER}), .ImmSel(control_logic_1_immsel), .imm(imm));
  // Probe on PCSel
  // Probe on RegWEn
  control_logic control_logic_1 (
    .CSRWen(CSRWen), .PCSel(PCSel), .RegWEn(RegWEn), .ImmSel(control_logic_1_immsel), .BrUn(brun),
    .ASel(ASel), .BSel(BSel), .ALUSel(ALUSel), .MemRW(MemRW), .WBSel(WBSel), .CSRSel(CSRSel),
    .inst({funct7, imm_20_31, INSTRUCTION_AFTER}), .BrEq(breq), .BrLt(brlt));
  // Probe on control_logic_1_immsel
  // Probe on breq
  // Probe on brun
  // Probe on INSTRUCTION
  Multiplexer #(.width(32)) multiplexer_3 (.in0(INSTRUCTION), .in1(32'h13), .out(multiplexer_3_out), .sel(PCSel));
  // Probe on PCSel
  // Probe on BSel
  // Probe on ASel
  Register #(.width(32)) IFID_inst (
    .D(multiplexer_3_out), .clk(clk), .Q({funct7, imm_20_31, INSTRUCTION_AFTER}));  // open: en, clr
  and and_1 (jal, INSTRUCTION[0], INSTRUCTION[1], INSTRUCTION[2], INSTRUCTION[3], ~INSTRUCTION[4], INSTRUCTION[5], INSTRUCTION[6]);  // AND_Gate
  and and_2 (jalr, INSTRUCTION[0], INSTRUCTION[1], INSTRUCTION[2], ~INSTRUCTION[3], ~INSTRUCTION[4], INSTRUCTION[5], INSTRUCTION[6]);  // AND_Gate
  // Probe on ALUSel
  // Probe on MemRW
  // Probe on WBSel
  Multiplexer #(.width(32)) multiplexer_4 (.in0(PC_AFTER), .in1(rs1_data), .out(multiplexer_4_out), .sel(ASel));
  Multiplexer #(.width(32)) multiplexer_5 (.in0(imm), .in1(WRITE_DATA), .out(multiplexer_5_out), .sel(BSel));
  // Probe on WRITE_ADDRESS
  alu alu_1 (
    .Result(WRITE_ADDRESS), .A(multiplexer_4_out), .B(multiplexer_5_out), .ALUSel(ALUSel));  // open: out_5, out_6
  Register #(.width(32)) IFID_pc (.D(PROGRAM_COUNTER), .clk(clk), .Q(PC_AFTER));  // open: en, clr
  assign WRITE_ENABLE = {{3{MemRW}}, MemRW};  // Bit_Extender bit_extender_1
  assign bit_extender_2_out = {{27{1'b0}}, INSTRUCTION_AFTER[19:15]};  // Bit_Extender bit_extender_2
  csr csr_1 (.CSR_address(12'h51e), .CSR_din(CSR_din), .CSR_WE(CSRWen), .clk(clk), .tohost(tohost));
  Multiplexer #(.width(32)) multiplexer_6 (.in0(bit_extender_2_out), .in1(rs1_data), .out(CSR_din), .sel(CSRSel));

  // Other names for the same wires on the sheet: aluresult[31:0] = WRITE_ADDRESS; opcode_cpu[6:0] = INSTRUCTION[6:0];
  //   rd[4:0] = INSTRUCTION_AFTER[11:7]; rs1[4:0] = INSTRUCTION_AFTER[19:15];
  //   INSTRUCTION_AFTER[31:20] = {funct7, imm_20_31}; rs2[4:0] = imm_20_31; imm_20_31[11:5] = funct7;
  //   immed[6:0] = funct7; rs2_data[31:0] = WRITE_DATA

  // Notes on the sheet:
  //   PCSel
  //   helper
  //   Output to IMEM
  //   IMEM (do **NOT** move this)
  //   Inputs from IMEM
  //   It is OK to move the PC, RegFile, ALU, MEM, Branch Comp, Imm Gen, and Control Logic to wherever is most convenient for you when constructing your CPU, and to delete this text
  //   Inputs/Outputs for testing. Do **NOT** move these.
  //   Outputs To DMEM
  //   CSR related
  //   DMEM (do **NOT** move this)
  //   Inputs From DMEM
  //   MemRW only emit 1bit, but as we know, the WRITE_ENABLE have 4bits, each bit corresponds to overwritten status of  one byte
  //   that means , when MemRW equals to 1, the WRITE_ENABLE equals to 0b1111, that's to say, the WRITE_ADDRESS will writes to DMEM all bytes. 
  //   when MemRW equals to 0, the WRITE_ENABLE equals to 0b0000, that's to say, the WRITE_ADDRESS will writes to DMEM all zero. that is read
  //   why the aluresult is going to write to WRITE_ADDRESS: for example `ld x1, offset(x2)`, this inst would calculate the address of addition of offset and x2, then this result emitted from alu is a address of mem, used to indexing the mem data 
endmodule
