// Logisim project imm-gen.circ as structural Verilog: 1 circuit, main circuit imm_gen
module imm_gen (
  input  [31:0] inst,
  input  [2:0] ImmSel,
  output [31:0] imm
);

  wire [31:0] I_type, S_type, SB_type;
  wire [31:20] UJ_type;

  // Probe on {inst[31:12], {12{1'b0}}}
  assign S_type = {{20{inst[31]}}, {inst[31:25], inst[11:7]}};  // Bit_Extender bit_extender_1
  // Probe on inst[11:8]
  // Probe on inst[7]
  // Probe on inst[30:25]
  // Probe on inst[7]
  // Probe on inst[31]
  assign SB_type = {{20{inst[7]}}, {inst[7], inst[30:25], inst[11:8], 1'b0}};  // Bit_Extender bit_extender_2
  // Probe on SB_type
  assign I_type = {{20{inst[31]}}, inst[31:20]};  // Bit_Extender bit_extender_3
  assign UJ_type = {{11{inst[31]}}, inst[31]};  // Bit_Extender bit_extender_4
  // Probe on {UJ_type, inst[19:12], inst[20], inst[30:21], 1'b0}
  Multiplexer #(.select(3), .width(32)) multiplexer_1 (
    .in0(I_type), .in1({inst[31:12], {12{1'b0}}}), .in2(S_type), .in3(SB_type),
    .in4({UJ_type, inst[19:12], inst[20], inst[30:21], 1'b0}), .in5({32{1'b0}}), .out(imm), .sel(ImmSel));  // open: in6, in7

  // Other names for the same wires on the sheet: U_type[31:12] = inst[31:12];
  //   UJ_type[19:1] = {inst[19:12], inst[20], inst[30:21]}

  // Notes on the sheet:
  //   INPUTS to your circuit
  //   this probe only for debug, view the value within lines. either the 5th and 6th bit can decide how the imm generated or ImmSel needed
  //   DON'T CHANGE THE LOCATIONS OF THE INPUTS AND OUTPUTS!
  //   OUTPUT from your circuit
endmodule
