// Logisim project regfile.circ as structural Verilog: 1 circuit, main circuit regfile
module regfile (
  input  [4:0] rs1,
  input  [4:0] rs2,
  input  [4:0] rd,
  input  [31:0] Write_Data,
  input  RegWEn,
  input  clk,
  output [31:0] ra,
  output [31:0] sp,
  output [31:0] t0,
  output [31:0] t1,
  output [31:0] t2,
  output [31:0] s0,
  output [31:0] s1,
  output [31:0] a0,
  output [31:0] Read_Data_1,
  output [31:0] Read_Data_2
);

  wire a0_we, a1_we, a2_we, a3_we, a4_we, a5_we, a6_we, a7_we, gp_we, ra_we, s0_we, s1_we, s2_we, s3_we,
       s4_we, s5_we, s6_we, s7_we, s8_we, s9_we, s10_we, s11_we, sp_we, t0_we, t1_we, t2_we, t3_we, t4_we,
       t5_we, t6_we, tp_we, x0_we;
  wire [31:0] a1_out, a2_out, a3_out, a4_out, a5_out, a6_out, a7_out, gp_out, s2_out, s3_out, s4_out, s5_out,
       s6_out, s7_out, s8_out, s9_out, s10_out, s11_out, t3_out, t4_out, t5_out, t6_out, tp_out, x0_out;

  Demultiplexer #(.enable("false"), .select(5)) demultiplexer_1 (
    .out0(x0_we), .out1(ra_we), .out2(sp_we), .out3(gp_we), .out4(tp_we), .out5(t0_we), .out6(t1_we),
    .out7(t2_we), .out8(s0_we), .out9(s1_we), .out10(a0_we), .out11(a1_we), .out12(a2_we), .out13(a3_we),
    .out14(a4_we), .out15(a5_we), .out16(a6_we), .out17(a7_we), .out18(s2_we), .out19(s3_we), .out20(s4_we),
    .out21(s5_we), .out22(s6_we), .out23(s7_we), .out24(s8_we), .out25(s9_we), .out26(s10_we),
    .out27(s11_we), .out28(t3_we), .out29(t4_we), .out30(t5_we), .out31(t6_we), .in(RegWEn), .sel(rd));
  Register #(.width(32)) rareg (.D(Write_Data), .en(ra_we), .clk(clk), .Q(ra));  // open: clr
  Register #(.width(32)) gpreg (.D(Write_Data), .en(gp_we), .clk(clk), .Q(gp_out));  // open: clr
  Register #(.width(32)) t0reg (.D(Write_Data), .en(t0_we), .clk(clk), .Q(t0));  // open: clr
  Register #(.width(32)) register_1 (.D(Write_Data), .en(t1_we), .clk(clk), .Q(t1));  // open: clr
  Register #(.width(32)) register_2 (.D(Write_Data), .en(s1_we), .clk(clk), .Q(s1));  // open: clr
  Register #(.width(32)) register_3 (.D(Write_Data), .en(a1_we), .clk(clk), .Q(a1_out));  // open: clr
  Register #(.width(32)) register_4 (.D(Write_Data), .en(a3_we), .clk(clk), .Q(a3_out));  // open: clr
  Register #(.width(32)) register_5 (.D(Write_Data), .en(a5_we), .clk(clk), .Q(a5_out));  // open: clr
  Register #(.width(32)) register_6 (.D(Write_Data), .en(a7_we), .clk(clk), .Q(a7_out));  // open: clr
  Register #(.width(32)) register_7 (.D(Write_Data), .en(s3_we), .clk(clk), .Q(s3_out));  // open: clr
  Register #(.width(32)) register_8 (.D(Write_Data), .en(s5_we), .clk(clk), .Q(s5_out));  // open: clr
  Register #(.width(32)) register_9 (.D(Write_Data), .en(s7_we), .clk(clk), .Q(s7_out));  // open: clr
  Register #(.width(32)) register_10 (.D(Write_Data), .en(s9_we), .clk(clk), .Q(s9_out));  // open: clr
  Register #(.width(32)) register_11 (.D(Write_Data), .en(s11_we), .clk(clk), .Q(s11_out));  // open: clr
  Register #(.width(32)) register_12 (.D(Write_Data), .en(t4_we), .clk(clk), .Q(t4_out));  // open: clr
  Register #(.width(32)) register_13 (.D(Write_Data), .en(t6_we), .clk(clk), .Q(t6_out));  // open: clr
  Register #(.width(32)) spreg (.D(Write_Data), .en(sp_we), .clk(clk), .Q(sp));  // open: clr
  Register #(.width(32)) tpreg (.D(Write_Data), .en(tp_we), .clk(clk), .Q(tp_out));  // open: clr
  Register #(.width(32)) register_14 (.D(Write_Data), .en(t2_we), .clk(clk), .Q(t2));  // open: clr
  Register #(.width(32)) register_15 (.D(Write_Data), .en(s0_we), .clk(clk), .Q(s0));  // open: clr
  Register #(.width(32)) register_16 (.D(Write_Data), .en(a0_we), .clk(clk), .Q(a0));  // open: clr
  Register #(.width(32)) register_17 (.D(Write_Data), .en(a2_we), .clk(clk), .Q(a2_out));  // open: clr
  Register #(.width(32)) register_18 (.D(Write_Data), .en(a4_we), .clk(clk), .Q(a4_out));  // open: clr
  Register #(.width(32)) register_19 (.D(Write_Data), .en(a6_we), .clk(clk), .Q(a6_out));  // open: clr
  Register #(.width(32)) register_20 (.D(Write_Data), .en(s2_we), .clk(clk), .Q(s2_out));  // open: clr
  Register #(.width(32)) register_21 (.D(Write_Data), .en(s4_we), .clk(clk), .Q(s4_out));  // open: clr
  Register #(.width(32)) register_22 (.D(Write_Data), .en(s6_we), .clk(clk), .Q(s6_out));  // open: clr
  Register #(.width(32)) register_23 (.D(Write_Data), .en(s8_we), .clk(clk), .Q(s8_out));  // open: clr
  Register #(.width(32)) register_24 (.D(Write_Data), .en(s10_we), .clk(clk), .Q(s10_out));  // open: clr
  Register #(.width(32)) register_25 (.D(Write_Data), .en(t3_we), .clk(clk), .Q(t3_out));  // open: clr
  Register #(.width(32)) register_26 (.D(Write_Data), .en(t5_we), .clk(clk), .Q(t5_out));  // open: clr
  Register #(.width(32)) register_27 (.D(Write_Data), .en(x0_we), .clk(clk), .Q(x0_out), .clr(1'b1));
  Multiplexer #(.enable("false"), .select(5), .width(32)) multiplexer_1 (
    .in0(x0_out), .in1(ra), .in2(sp), .in3(gp_out), .in4(tp_out), .in5(t0), .in6(t1), .in7(t2), .in8(s0),
    .in9(s1), .in10(a0), .in11(a1_out), .in12(a2_out), .in13(a3_out), .in14(a4_out), .in15(a5_out),
    .in16(a6_out), .in17(a7_out), .in18(s2_out), .in19(s3_out), .in20(s4_out), .in21(s5_out), .in22(s6_out),
    .in23(s7_out), .in24(s8_out), .in25(s9_out), .in26(s10_out), .in27(s11_out), .in28(t3_out),
    .in29(t4_out), .in30(t5_out), .in31(t6_out), .out(Read_Data_1), .sel(rs1));
  Multiplexer #(.enable("false"), .select(5), .width(32)) multiplexer_2 (
    .in0(x0_out), .in1(ra), .in2(sp), .in3(gp_out), .in4(tp_out), .in5(t0), .in6(t1), .in7(t2), .in8(s0),
    .in9(s1), .in10(a0), .in11(a1_out), .in12(a2_out), .in13(a3_out), .in14(a4_out), .in15(a5_out),
    .in16(a6_out), .in17(a7_out), .in18(s2_out), .in19(s3_out), .in20(s4_out), .in21(s5_out), .in22(s6_out),
    .in23(s7_out), .in24(s8_out), .in25(s9_out), .in26(s10_out), .in27(s11_out), .in28(t3_out),
    .in29(t4_out), .in30(t5_out), .in31(t6_out), .out(Read_Data_2), .sel(rs2));

  // Other names for the same wires on the sheet: a0_out[31:0] = a0; ra_out[31:0] = ra; read_data1[31:0] = Read_Data_1;
  //   read_data2[31:0] = Read_Data_2; read_reg1[4:0] = rs1; read_reg2[4:0] = rs2; s0_out[31:0] = s0;
  //   s1_out[31:0] = s1; sp_out[31:0] = sp; t0_out[31:0] = t0; t1_out[31:0] = t1; t2_out[31:0] = t2;
  //   write_en = RegWEn; write_reg[4:0] = rd

  // Notes on the sheet:
  //   INPUTS to your circuit
  //   DON'T CHANGE THE LOCATIONS OF THE INPUTS AND OUTPUTS!
  //   These are DEBUG/TEST outputs from your circuit.
  //   OUTPUTS from your circuit
endmodule
